# Fritzing sketch Aquarium (saved by Fritzing 0.9.3b)
breadboards: 1

parts:
  Bauteil1 = Arduino Uno (Rev3) - ICSP
  LED2 = LED - 5mm [color="Blue (525nm)" part_number=MAIN_WATER_SUPPLY_VALVE package="5 mm [THT]"]
  LED3 = LED - 5mm [color="Yellow (595nm)" part_number=WATER_DRAIN_VALVE package="5 mm [THT]"]
  S1 = Momentary Switch [part_number=WATER_LEAK_SENSOR package=ksa_sealed_tac_switch]
  S2 = Momentary Switch [part_number=TEMPERATURE_SENSOR package=ksa_sealed_tac_switch]
  S3 = Momentary Switch [part_number=LOW_LEVEL_SENSOR package=ksa_sealed_tac_switch]
  S4 = Momentary Switch [part_number=HIGH_LEVEL_SENSOR package=ksa_sealed_tac_switch]
  R1 = Resistor [tolerance=±5% resistance=220 package=THT]
  R2 = Resistor [tolerance=±5% resistance=220 package=THT]
  R3 = Resistor [tolerance=±5% resistance=220 package=THT]
  R4 = Resistor [tolerance=±5% resistance=220 package=THT]
  LED4 = LED - 5mm [color="Green (570nm)" part_number=WATER_FILL_VALVE package="5 mm [THT]"]
  LED5 = LED - 5mm [color="Red (635nm)" part_number=EMERGENCY_LIGHT package="5 mm [THT]"]

nets:
  N1: Bauteil1.D8, R2.Pin_1
  N2: Bauteil1.D9_PWM, R1.Pin_1
  N3: Bauteil1.GND, LED2.cathode, LED3.cathode, S1.1, S2.1, S3.1, S4.1, LED4.cathode, LED5.cathode
  N4: Bauteil1.D2, S1.3
  N5: Bauteil1.D3_PWM, S2.3
  N6: Bauteil1.D4, S3.3
  N7: Bauteil1.D5_PWM, S4.3
  N8: Bauteil1.D6_PWM, R4.Pin_1
  N9: Bauteil1.D7, R3.Pin_1
  N10: LED2.anode, R3.Pin_0
  N11: LED3.anode, R2.Pin_0
  N12: R1.Pin_0, LED4.anode
  N13: R4.Pin_0, LED5.anode
